// Logisim project sketch.circ as structural Verilog
module main (
);

  wire button_out, clk, clock_1_out, clr, lw, on, sw;
  wire [7:0] cpu_1_ram_address, cpu_1_ram_dbus, undriven;

  Clock clock_1 (.out(clock_1_out));
  Button button (.out(button_out));
  switch switch_1 (.in_1(button_out), .out_2(on));
  Button u_clr (.out(clr));
  assign clk = on ? clock_1_out : 1'bz;  // Controlled_Buffer controlled_buffer_1
  CPU cpu_1 (.clr(clr), .clk(clk), .Data_In(undriven), .RAM_dbus(cpu_1_ram_dbus), .RAM_Address(cpu_1_ram_address));
  RAM #(.bus("separate")) ram_1 (
    .addr(cpu_1_ram_address), .din(undriven), .data(cpu_1_ram_dbus), .str(sw), .clk(clk), .ld(lw), .clr(clr));  // open: sel
endmodule

module CPU (
  input  clr,
  input  clk,
  input  [7:0] Data_In,
  output [7:0] RAM_dbus,
  output [7:0] RAM_Address
);
endmodule

module Regs (
  input  clk,
  input  [7:0] Reg_Write,
  input  [2:0] in_3,
  input  [2:0] in_4,
  output [7:0] out_5
);

  wire [7:0] demultiplexer_1_out0, demultiplexer_1_out1, demultiplexer_1_out2, demultiplexer_1_out3,
       demultiplexer_1_out4, demultiplexer_1_out5, demultiplexer_1_out6, demultiplexer_1_out7, register_1_q,
       register_2_q, register_3_q, register_4_q, register_5_q, register_6_q, register_7_q, register_8_q;

  Demultiplexer #(.select(3), .width(8)) demultiplexer_1 (
    .out0(demultiplexer_1_out0), .out1(demultiplexer_1_out1), .out2(demultiplexer_1_out2),
    .out3(demultiplexer_1_out3), .out4(demultiplexer_1_out4), .out5(demultiplexer_1_out5),
    .out6(demultiplexer_1_out6), .out7(demultiplexer_1_out7), .in(Reg_Write), .sel(in_3));  // open: en
  Register register_1 (.D(demultiplexer_1_out0), .Q(register_1_q), .clk(clk));  // open: en, clr
  Register register_2 (.D(demultiplexer_1_out1), .Q(register_2_q), .clk(clk));  // open: en, clr
  Register register_3 (.D(demultiplexer_1_out2), .Q(register_3_q), .clk(clk));  // open: en, clr
  Register register_4 (.D(demultiplexer_1_out3), .Q(register_4_q), .clk(clk));  // open: en, clr
  Register register_5 (.D(demultiplexer_1_out4), .Q(register_5_q), .clk(clk));  // open: en, clr
  Register register_6 (.D(demultiplexer_1_out5), .Q(register_6_q), .clk(clk));  // open: en, clr
  Register register_7 (.D(demultiplexer_1_out6), .Q(register_7_q), .clk(clk));  // open: en, clr
  Register register_8 (.D(demultiplexer_1_out7), .Q(register_8_q), .clk(clk));  // open: en, clr
  Multiplexer #(.select(3), .width(8)) multiplexer_1 (
    .in0(register_1_q), .in1(register_2_q), .in2(register_3_q), .in3(register_4_q), .in4(register_5_q),
    .in5(register_6_q), .in6(register_7_q), .in7(register_8_q), .out(out_5), .sel(in_4));  // open: en
endmodule

module ALU (
);

  wire [7:0] ram_1_data, undriven, undriven_2;

  RAM #(.bus("separate")) ram_1 (.addr(undriven), .din(undriven_2), .data(ram_1_data));  // open: str, sel, clk, ld, clr
endmodule

module switch (
  input  in_1,
  output out_2
);

  wire d_ff_1_qn;

  D_Flip_Flop d_ff_1 (.clk(in_1), .D(d_ff_1_qn), .Q(out_2), .Qn(d_ff_1_qn));  // open: preset, en, reset
endmodule
